// Logisim project EX2-Q1.circ as structural Verilog: 1 circuit, main circuit main
module main (
  input  e0,
  input  e1,
  input  c,
  output s
);

  Multiplexer multiplexer_1 (.in0(e0), .in1(e1), .out(s), .sel(c));  // open: en
endmodule
