// Logisim project EX5-Q1.circ as structural Verilog: 3 circuits, main circuit main
module main (
  input  in_1,
  input  in_2,
  input  in_3,
  output out_4,
  output out_5
);

  Adder #(.width(1)) adder_1 (.a(in_2), .b(in_3), .out(out_5), .cin(in_1), .cout(out_4));
endmodule

module d (
  input  in_1,
  input  in_2,
  input  in_3,
  input  in_4,
  input  in_5,
  input  in_6,
  input  in_7,
  input  in_8,
  input  in_9,
  output out_10,
  output out_11,
  output out_12,
  output out_13,
  output out_14
);

  wire adder_1_cout, adder_2_cout, adder_3_cout, xor_1_out;

  xor xor_1 (xor_1_out, in_1, in_3);
  Adder #(.width(1)) adder_1 (.a(in_2), .b(xor_1_out), .out(out_10), .cin(in_1), .cout(adder_1_cout));
  Adder #(.width(1)) adder_2 (.a(in_4), .b(in_5), .out(out_11), .cin(adder_1_cout), .cout(adder_2_cout));
  Adder #(.width(1)) adder_3 (.a(in_6), .b(in_7), .out(out_12), .cin(adder_2_cout), .cout(adder_3_cout));
  Adder #(.width(1)) adder_4 (.a(in_8), .b(in_9), .out(out_13), .cin(adder_3_cout), .cout(out_14));
endmodule

module c (
  input  in_1,
  input  in_2,
  input  in_3,
  input  in_4,
  input  in_5,
  input  in_6,
  input  in_7
);

  d d_1 (
    .in_6(in_4), .in_7(in_5), .in_8(in_6), .in_9(in_7));  // open: in_1, in_2, in_3, in_4, in_5, out_10, out_11, out_12, out_13, out_14
endmodule
