// Logisim project EX3-Q1.circ as structural Verilog: 3 circuits, main circuit main
module main (
  input  in_1,
  input  in_2,
  input  in_3,
  input  in_4,
  input  in_5,
  input  in_6,
  input  in_7,
  output out_8
);

  wire multiplexer_1_out, multiplexer_2_out;

  Multiplexer multiplexer_1 (.in0(in_1), .in1(in_2), .out(multiplexer_1_out), .sel(in_3));  // open: en
  Multiplexer multiplexer_2 (.in0(in_4), .in1(in_5), .out(multiplexer_2_out), .sel(in_7));  // open: en
  Multiplexer multiplexer_3 (.in0(multiplexer_1_out), .in1(multiplexer_2_out), .out(out_8), .sel(in_6));  // open: en
endmodule

module m (
  input  c,
  input  e0,
  input  e1,
  output out_4
);

  wire and_1_out, and_2_out;

  and and_1 (and_1_out, e1, c);
  and and_2 (and_2_out, e0, ~c);  // AND_Gate
  or or_1 (out_4, and_1_out, and_2_out);
endmodule

module circuit (
  input  in_1,
  input  in_2,
  input  in_3,
  input  in_4,
  input  in_5,
  input  in_6,
  input  in_7,
  output out_8
);

  wire and_1_out, and_2_out, m_1_out_4, m_2_out_4;

  m m_1 (.c(in_3), .e0(in_2), .e1(in_1), .out_4(m_1_out_4));
  m m_2 (.c(in_7), .e0(in_6), .e1(in_4), .out_4(m_2_out_4));
  and and_1 (and_1_out, m_1_out_4, in_5);
  and and_2 (and_2_out, in_5, m_2_out_4);
  or or_1 (out_8, and_1_out, and_2_out);
endmodule
